# Fritzing sketch q2w-i2c-direct-connection (saved by Fritzing 0.9.3b)

parts:
  Raspberry_Pi_1 = Raspberry Pi 3 [part_number=RPI-3-V1.2]
  J1 = shrouded pin header, 6 pins [form="♂ (shrouded male)"]

nets:
  N1: Raspberry_Pi_1.3v3, J1.pin6
  N2: Raspberry_Pi_1.GPIO2, J1.pin2
  N3: Raspberry_Pi_1.GPIO3, J1.pin5
  N4: Raspberry_Pi_1.GND, J1.pin3

notes:
  gap >>
